# Fritzing sketch Schema (saved by Fritzing 0.9.7b)
circuit board: 8.46667cm x 5.64444cm
breadboards: 1

parts:
  Composant3 = Arduino Nano (Rev3.0)
  DFRobot_DFPlayer_Mini4 = DFRobot DFPlayer Mini [part_number=DFR0299]
  SP4 = SPEAKER [package=pcb_mount_speaker]
  S39 = Pushbutton [package=THT]
  S33 = Pushbutton [package=THT]
  S40 = Pushbutton [package=THT]
  S38 = Pushbutton [package=THT]
  S36 = Pushbutton [package=THT]
  S31 = Pushbutton [package=THT]
  S32 = Pushbutton [package=THT]
  S35 = Pushbutton [package=THT]
  S37 = Pushbutton [package=THT]
  S30 = Pushbutton [package=THT]
  VCC1 = Battery

nets:
  N1: Composant3.GND, DFRobot_DFPlayer_Mini4.GND-1, DFRobot_DFPlayer_Mini4.GND-2, S39.leg1, S33.leg1, S40.leg1, S38.leg1, S36.leg1, S31.leg1, S32.leg1, S35.leg1, S37.leg1, S30.leg1, VCC1.-
  N2: Composant3.D2, S31.leg0
  N3: Composant3.D3, S35.leg0
  N4: Composant3.D4, S37.leg0
  N5: Composant3.D5, S38.leg0
  N6: Composant3.D6, S33.leg0
  N7: Composant3.D7, S32.leg0
  N8: Composant3.D8, S36.leg0
  N9: Composant3.D9, S30.leg0
  N10: Composant3.D10, S39.leg0
  N11: Composant3.D11/MOSI, S40.leg0
  N12: Composant3.VIN, VCC1.+
  N13: Composant3.A1, DFRobot_DFPlayer_Mini4.RX
  N14: Composant3.A0, DFRobot_DFPlayer_Mini4.TX
  3V3: Composant3.3V3, DFRobot_DFPlayer_Mini4.VCC
  N15: DFRobot_DFPlayer_Mini4.SPK_1, SP4.-
  N16: DFRobot_DFPlayer_Mini4.SPK_2, SP4.+
