# Fritzing sketch Schema_Arduino_Nano (saved by Fritzing 0.9.9b)
breadboards: 1

parts:
  DFRobot_DFPlayer_Mini1 = DFRobot DFPlayer Mini [part_number=DFR0299]
  Composant1 = Arduino Nano (Rev3.0)
  SP1 = SPEAKER [package=pcb_mount_speaker]
  R1 = Resistor [tolerance=±5% power=0.25 resistance=1k package=THT]
  S1 = SWITCH-MOMENTARY-2 [package=tactile-switch-1101ne]

nets:
  VCC: DFRobot_DFPlayer_Mini1.VCC, Composant1.5V
  N1: DFRobot_DFPlayer_Mini1.TX, Composant1.D10
  N2: DFRobot_DFPlayer_Mini1.SPK_1, SP1.-
  N3: DFRobot_DFPlayer_Mini1.GND-1, DFRobot_DFPlayer_Mini1.GND-2, Composant1.GND, S1.2
  N4: DFRobot_DFPlayer_Mini1.SPK_2, SP1.+
  N5: Composant1.D11/MOSI, R1.Pin_1
  N6: Composant1.A3, S1.1

notes:
  Détection décrochage
  (masse partagée avec le cadran)
  Combiné
  A
  B
  C
  D
  Cadran rotatif
  Arduino
  Nano
  DFPlayer
  (Lecteur MP3)
  E
  F
  G
