# Fritzing sketch Schema_Seeduino_Xiao (saved by Fritzing 0.9.9b)
breadboards: 1

parts:
  DFRobot_DFPlayer_Mini1 = DFRobot DFPlayer Mini [part_number=DFR0299]
  SP1 = SPEAKER [package=pcb_mount_speaker]
  R1 = Resistor [tolerance=±5% power=0.25 resistance=1k package=THT]
  S1 = SWITCH-MOMENTARY-2 [package=tactile-switch-1101ne]
  Mod1 = seeeduino-xiao_1

nets:
  N1: DFRobot_DFPlayer_Mini1.VCC, S1.2
  N2: DFRobot_DFPlayer_Mini1.TX, Mod1.connector9
  N3: DFRobot_DFPlayer_Mini1.SPK_1, SP1.-
  N4: DFRobot_DFPlayer_Mini1.GND-1, DFRobot_DFPlayer_Mini1.GND-2, SP1.+
  N5: R1.Pin_1, Mod1.connector10
  N6: S1.1, Mod1.connector3

notes:
  Détection décrochage
  (masse globale)
  Combiné
  (masse globale)
  A
  B
  C
  D
  Cadran rotatif
  Seeduino
  Xiao
  DFPlayer
  (Lecteur MP3)
  E
  F
