# Fritzing sketch PN532 (saved by Fritzing 0.9.9b)

parts:
  Composant1 = PN532 Elechouse RFID NFC Module V3
  Mod1 = seeeduino-xiao

nets:
  GND: Composant1.GND, Mod1.GND
  VCC: Composant1.VCC, Mod1.5V
  N1: Composant1.SDA, Mod1.D4
  N2: Composant1.SCL, Mod1.D5

notes:
  0
  1
  A DROITE
  A GAUCHE

custom parts:
  PN532 Elechouse RFID NFC Module V3: NFC is a popular technology in recent years. We often heard this work while smart phone company such as Samsung or HTC introduces their latest high-end phones. Almost all the high-end phone in the market support NFC. Near field communication (NFC) is a set of standards for smart phones and similar devices to establish radio communication with each other by touching them together or bringing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
  seeeduino-xiao: Seeeduino XIAO processor board.
